# Fritzing sketch sailboatSchematics (saved by Fritzing 0.9.3b)
breadboards: 1

parts:
  Part1 = Arduino Mega 2560 (Rev3)
  U3 = EM408_CON [package=em408_con]
  Part2 = Compass Module - HMC6352
  Part3 = 9 Degrees of Freedom - Sensor Stick  # not connected
  FLO-30_Circuit1 = FLO-30 Circuit  # not connected

nets:
  N1: Part1.D21/SCL, Part2.SCL
  N2: Part1.D20/SDA, Part2.SDA
  N3: Part1.D15/RX3, U3.RX
  3V3: Part1.3V3, Part2.VCC
  5V: Part1.5V, U3.VCC
  GND: Part1.GND, U3.GND, Part2.GND

// code stored in the sketch: blink_example.ino

